# Fritzing sketch ADC vs ADN (saved by Fritzing 0.9.3b)
breadboards: 1

parts:
  Part4 = Arduino Mega 2560 (Rev3)
  AC_To_DC_1 = ADMP504 - Ultralow Noise Microphone with Bottom Port and Analog Output [part_number=ADMP504]

nets:
  N1: Part4.GND, AC_To_DC_1.OUTPUT
  N2: Part4.D11_PWM, AC_To_DC_1.GND
