# Fritzing sketch Adn vs power (saved by Fritzing 0.9.3b)
breadboards: 1

parts:
  DC_in = Power Jack [package=power_jack_smd]
  Part4 = Arduino Mega 2560 (Rev3)

nets:
  GND: DC_in.GND, Part4.GND
  N1: DC_in.GNDBREAK, Part4.VIN
