# Fritzing sketch RELAY PUMP ADC DC (saved by Fritzing 0.9.3b)
breadboards: 1

parts:
  RELAY = RELAY [package=relay-jzc]
  AC = AC Power [voltage=220 frequency=60]
  PUMP = DC Motor
  AC_To_DC = ADMP504 - Ultralow Noise Microphone with Bottom Port and Analog Output [part_number=ADMP504]

nets:
  N1: RELAY.NC, PUMP.pin_1, AC_To_DC.NC
  N2: RELAY.MAIN, AC.V-
  N3: AC.V+, PUMP.pin_2
