# Fritzing sketch SWP_Arduino vs RTC (saved by Fritzing 0.9.3b)

parts:
  Part4 = Arduino Mega 2560 (Rev3)
  DS1308 = Real Time Clock Module - DS1307 RTC Breakout Board

nets:
  N1: Part4.D21/SCL, Part4.SCL, DS1308.SCL
  N2: Part4.D20/SDA, Part4.SDA, DS1308.SDA
  5V: Part4.5V, DS1308.5V
  GND: Part4.GND, DS1308.GND
