# Fritzing sketch Sim vs Arduino (saved by Fritzing 0.9.3b)
breadboards: 1

parts:
  Part4 = Arduino Mega 2560 (Rev3)
  SIM_800A = SIM800L [package=THT]

nets:
  GND: Part4.GND, SIM_800A.GND
  VIN: Part4.VIN, SIM_800A.VDD
  N1: Part4.D50, SIM_800A.SIM_TXD
  N2: Part4.D51, SIM_800A.SIM_RXD
