# Fritzing sketch Sim vs power (saved by Fritzing 0.9.3b)
breadboards: 1

parts:
  SIM_800A = SIM800L [package=THT]
  Power = Power Jack [package=power_jack_smd]

nets:
  N1: SIM_800A.VDD, Power.GNDBREAK
  GND: SIM_800A.GND, Power.GND
