# Fritzing sketch adn+relay (saved by Fritzing 0.9.3b)
breadboards: 1

parts:
  Part4 = Arduino Mega 2560 (Rev3)
  Relay = RELAY [package=relay-jzc]

nets:
  N1: Part4.GND, Relay.COIL2
  N2: Part4.D12_PWM, Relay.COIL1
